# Fritzing sketch HauntedPumpkinSketchwithaudiojack (saved by Fritzing 0.7.10b)
breadboards: 1

parts:
  Arduino1 = Arduino
  R1 = Resistor [tolerance=±5% resistance=200 package=THT]
  LED1 = LED - 5mm [color="Orange (620nm)" package="5 mm [THT]"]
  LED2 = LED - 5mm [color="Red (633nm)" package="5 mm [THT]"]
  R2 = Resistor [tolerance=±5% resistance=200 package=THT]
  TRS1 = Stereo Jack (TRS) 3.5mm [package="PG203J [THT]"]
  U1 = IC, SIP package, 4 pins [chip_label=IC]

nets:
  N1: Arduino1.D12, U1.pin3
  N2: Arduino1.D9, U1.pin2
  N3: Arduino1.D7, R1.Pin_1
  N4: Arduino1.D5, R2.Pin_1
  N5: Arduino1.+5V, TRS1.Sleeve, U1.pin1
  N6: Arduino1.GND, LED1.anode, LED2.anode, U1.pin4
  N7: R1.Pin_0, LED2.cathode
  N8: LED1.cathode, R2.Pin_0

notes:
  "IC" part is a placeholder for the HC-SR04 ultrasonic
  Wiring from L to R is:
  VCC (power)
  Trigger
  Echo
  Ground
  audio jack --->
